# Fritzing sketch circuit (saved by Fritzing 1.0.1rc)
circuit board: 16.2255cm x 10.5701cm
breadboards: 1

parts:
  R2 = Resistor [tolerance=±5% power=0.25 resistance=100 package=THT]
  R1 = Resistor [tolerance=±5% power=0.25 resistance=220 package=THT]
  R3 = Resistor [tolerance=±5% power=0.25 resistance=100 package=THT]
  LCD1 = LCD screen  # not connected
  Button_Previous_Page = Pushbutton [package="[THT]"]
  Arduino_Nano_33_BLE = Arduino Nano (Rev3.0) (ICSP)
  part = Grove OLED 128x96
  BME680 = Adafruit BME680 [part_number="Adafruit #3660"]
  part_2 = Grove 3 Axis Digital Accelerometer 16g
  LED1 = RGB LED (com. cathode, rbg) [package="5 mm [THT]"]
  Button_Next_Page = Pushbutton [package="[THT]"]
  Button_Mode = Pushbutton [package="[THT]"]

nets:
  N1: R2.Pin_0, Arduino_Nano_33_BLE.A1
  N2: R2.Pin_1, LED1.blue_anode
  N3: R1.Pin_0, Arduino_Nano_33_BLE.A0
  N4: R1.Pin_1, LED1.red_anode
  N5: R3.Pin_0, Arduino_Nano_33_BLE.A2
  N6: R3.Pin_1, LED1.green_anode
  GND: Button_Previous_Page.Pin_1, Button_Previous_Page.Pin_2, Arduino_Nano_33_BLE.GND, part.GND, BME680.GND, part_2.GND, LED1.common_cathode, Button_Next_Page.Pin_1, Button_Next_Page.Pin_2, Button_Mode.Pin_1, Button_Mode.Pin_2
  N7: Button_Previous_Page.Pin_3, Button_Previous_Page.Pin_4, Arduino_Nano_33_BLE.D4
  N8: Arduino_Nano_33_BLE.D2, Button_Mode.Pin_3, Button_Mode.Pin_4
  N9: Arduino_Nano_33_BLE.D3, Button_Next_Page.Pin_3, Button_Next_Page.Pin_4
  N10: Arduino_Nano_33_BLE.A5, part.SCL, BME680.SCK/SCL, part_2.SCL
  N11: Arduino_Nano_33_BLE.A4, part.SDA, BME680.SDI/SDA, part_2.SDA
  VCC: Arduino_Nano_33_BLE.3V3, part.VCC, BME680.VCC, part_2.VCC

notes:
  /SCL
  /SDA
