# Fritzing sketch circuit (saved by Fritzing 1.0.1rc)
circuit board: 14.1689cm x 10.3656cm
breadboards: 1

parts:
  R2 = Resistor [tolerance=±5% power=0.25 resistance=100 package=THT]
  R1 = Resistor [tolerance=±5% power=0.25 resistance=220 package=THT]
  R3 = Resistor [tolerance=±5% power=0.25 resistance=100 package=THT]
  part = LCD screen  # not connected
  S1 = Pushbutton [package="[THT]"]
  Arduino_Nano_33_BLE = Arduino Nano (Rev3.0) (ICSP)
  Grove_-_16x2_LCD1 = Grove OLED 128x96
  BME680 = Adafruit BME680 [part_number="Adafruit #3660"]
  part_2 = Grove 3 Axis Digital Accelerometer 16g
  LED1 = RGB LED (com. cathode, rbg) [package="5 mm [THT]"]

nets:
  N1: R2.Pin_0, Arduino_Nano_33_BLE.A1
  N2: R2.Pin_1, LED1.blue_anode
  N3: R1.Pin_0, Arduino_Nano_33_BLE.A0
  N4: R1.Pin_1, LED1.red_anode
  N5: R3.Pin_0, Arduino_Nano_33_BLE.A2
  N6: R3.Pin_1, LED1.green_anode
  GND: S1.Pin_1, S1.Pin_2, Arduino_Nano_33_BLE.GND, Grove_-_16x2_LCD1.GND, BME680.GND, part_2.GND, LED1.common_cathode
  N7: S1.Pin_3, S1.Pin_4, Arduino_Nano_33_BLE.D2
  N8: Arduino_Nano_33_BLE.A5, Grove_-_16x2_LCD1.SCL, BME680.SCK/SCL, part_2.SCL
  N9: Arduino_Nano_33_BLE.A4, Grove_-_16x2_LCD1.SDA, BME680.SDI/SDA, part_2.SDA
  VCC: Arduino_Nano_33_BLE.3V3, Grove_-_16x2_LCD1.VCC, BME680.VCC, part_2.VCC

notes:
  /SCL
  /SDA
